// Logisim project Project (final).circ as structural Verilog: 7 circuits, main circuit main
module main (
  input  Reset
);

  wire alu_1_zero, and_1_out, Clock_out, ctr_unit_1_alu_src, ctr_unit_1_branch, ctr_unit_1_ext_op,
       ctr_unit_1_jump, ctr_unit_1_mem_to_reg, ctr_unit_1_mem_write, ctr_unit_1_reg_ds, ctr_unit_1_reg_write,
       not_1_out;
  wire [2:0] alu_ctr_1_alu_op;
  wire [4:0] multiplexer_1_out;
  wire [15:0] alu_1_result;
  wire [31:0] adder_1_out, adder_2_out, extension_1_ext, extention_jump_1_ext_jump, multiplexer_2_out,
       multiplexer_3_out, multiplexer_4_out, multiplexer_5_out, PC_q, ram_1_data, ram_2_data,
       reg_file_1_read_data_1, reg_file_1_read_data_2, shifter_1_out;
  wire [31:16] alu_1_result_2;

  Clock Clock (.out(Clock_out));
  Register #(.width(32)) PC (.D(multiplexer_3_out), .Q(PC_q), .clk(Clock_out), .clr(Reset));  // open: en
  Adder #(.width(32)) adder_1 (.a(PC_q), .b(32'h1), .out(adder_1_out));  // open: cin, cout
  RAM #(.addrWidth(16), .dataWidth(32), .bus("separate")) ram_1 (
    .addr(PC_q[15:0]), .data(ram_1_data), .ld(1'b1));  // open: din, str, sel, clk, clr
  Ctr_Unit ctr_unit_1 (
    .Reg_Ds(ctr_unit_1_reg_ds), .Reg_Write(ctr_unit_1_reg_write), .ALU_Src(ctr_unit_1_alu_src),
    .Mem_to_Reg(ctr_unit_1_mem_to_reg), .Mem_Write(ctr_unit_1_mem_write), .Ext_Op(ctr_unit_1_ext_op),
    .Branch(ctr_unit_1_branch), .Jump(ctr_unit_1_jump), .Instruction(ram_1_data));
  ALU_Ctr alu_ctr_1 (.Function(ram_1_data[5:0]), .OP_Code(ram_1_data[31:26]), .ALU_OP(alu_ctr_1_alu_op));
  Multiplexer #(.width(5), .enable("false")) multiplexer_1 (
    .in0(ram_1_data[20:16]), .in1(ram_1_data[15:11]), .out(multiplexer_1_out), .sel(ctr_unit_1_reg_ds));
  Extension extension_1 (.Ext(extension_1_ext), .Imm(ram_1_data[15:0]), .Ext_Op(ctr_unit_1_ext_op));
  Reg_File reg_file_1 (
    .Data(multiplexer_5_out), .Reg_Write(ctr_unit_1_reg_write), .Read_Data_1(reg_file_1_read_data_1),
    .Read_Data_2(reg_file_1_read_data_2), .Write_Reg(multiplexer_1_out), .Read_Reg_1(ram_1_data[25:21]),
    .Read_Reg_2(ram_1_data[20:16]));
  Extention_Jump extention_jump_1 (.Target(ram_1_data[25:0]), .Ext_Jump(extention_jump_1_ext_jump));
  Multiplexer #(.width(32), .enable("false")) multiplexer_2 (
    .in0(reg_file_1_read_data_2), .in1(extension_1_ext), .out(multiplexer_2_out), .sel(ctr_unit_1_alu_src));
  ALU alu_1 (
    .Input_1(reg_file_1_read_data_1), .Input_2(multiplexer_2_out), .Result({alu_1_result_2, alu_1_result}),
    .ALU_Op(alu_ctr_1_alu_op), .Zero(alu_1_zero));
  Shifter #(.width(32)) shifter_1 (.in(extension_1_ext), .\dist (5'b00010), .out(shifter_1_out));
  Adder #(.width(32)) adder_2 (.a(adder_1_out), .b(shifter_1_out), .out(adder_2_out));  // open: cin, cout
  and and_1 (and_1_out, alu_1_zero, ctr_unit_1_branch);
  Multiplexer #(.width(32), .enable("false")) multiplexer_3 (
    .in0(multiplexer_4_out), .in1(extention_jump_1_ext_jump), .out(multiplexer_3_out), .sel(ctr_unit_1_jump));
  Multiplexer #(.width(32), .enable("false")) multiplexer_4 (
    .in0(adder_1_out), .in1(adder_2_out), .out(multiplexer_4_out), .sel(and_1_out));
  RAM #(.addrWidth(16), .dataWidth(32), .bus("separate")) ram_2 (
    .addr(alu_1_result), .data(ram_2_data), .str(ctr_unit_1_mem_write), .clk(not_1_out), .ld(1'b1));  // open: din, sel, clr
  not not_1 (not_1_out, Clock_out);
  Multiplexer #(.width(32), .enable("false")) multiplexer_5 (
    .in0({alu_1_result_2, alu_1_result}), .in1(ram_2_data), .out(multiplexer_5_out),
    .sel(ctr_unit_1_mem_to_reg));

  // Notes on the sheet:
  //   Reg Ds
  //   Shift Left 2
  //   Branch
  //   Jump
endmodule

module ALU (
  input  [31:0] Input_1,
  input  [31:0] Input_2,
  input  [2:0] ALU_Op,
  output Zero,
  output [31:0] Result
);

  wire and_2_out, not_1_out, not_2_out, not_3_out, not_4_out, not_5_out, not_6_out, not_7_out, not_8_out,
       not_9_out, not_10_out, not_11_out, not_12_out, not_13_out, not_14_out, not_15_out, not_16_out,
       not_17_out, not_18_out, not_19_out, not_20_out, not_21_out, not_22_out, not_23_out, not_24_out,
       not_25_out, not_26_out, not_27_out, not_28_out, not_29_out, not_30_out, not_31_out, not_32_out;
  wire [31:0] adder_1_out, And_out, divider_1_out, multiplier_1_out, Or_out, subtractor_1_out,
       subtractor_2_out;

  assign And_out = Input_2 & Input_1;  // AND_Gate And, 32 bits wide
  assign Or_out = Input_2 | Input_1;  // OR_Gate Or, 32 bits wide
  Adder #(.width(32)) adder_1 (.a(Input_2), .b(Input_1), .out(adder_1_out));  // open: cin, cout
  Subtractor #(.width(32)) subtractor_1 (.a(Input_2), .b(Input_1), .out(subtractor_1_out));  // open: bin, bout
  Multiplier #(.width(32)) multiplier_1 (.a(Input_2), .b(Input_1), .out(multiplier_1_out));  // open: cin, cout
  Divider #(.width(32)) divider_1 (.a(Input_2), .b(Input_1), .out(divider_1_out));  // open: upper, rem
  Subtractor #(.width(32)) subtractor_2 (.a(Input_1), .b(Input_2), .out(subtractor_2_out));  // open: bin, bout
  Multiplexer #(.select(3), .width(32), .enable("false")) multiplexer_1 (
    .in0(And_out), .in1(Or_out), .in2(adder_1_out), .in3(subtractor_1_out), .in4(multiplier_1_out),
    .in5(divider_1_out), .in6({32{1'b0}}), .in7({32{1'b0}}), .out(Result), .sel(ALU_Op));
  or or_2 (Zero, 1'b0, and_2_out);
  not not_1 (not_1_out, subtractor_2_out[0]);
  not not_2 (not_2_out, subtractor_2_out[1]);
  not not_3 (not_3_out, subtractor_2_out[30]);
  not not_4 (not_4_out, subtractor_2_out[31]);
  not not_5 (not_5_out, subtractor_2_out[2]);
  not not_6 (not_6_out, subtractor_2_out[3]);
  not not_7 (not_7_out, subtractor_2_out[4]);
  not not_8 (not_8_out, subtractor_2_out[5]);
  not not_9 (not_9_out, subtractor_2_out[6]);
  not not_10 (not_10_out, subtractor_2_out[7]);
  not not_11 (not_11_out, subtractor_2_out[8]);
  not not_12 (not_12_out, subtractor_2_out[9]);
  not not_13 (not_13_out, subtractor_2_out[23]);
  not not_14 (not_14_out, subtractor_2_out[24]);
  not not_15 (not_15_out, subtractor_2_out[25]);
  not not_16 (not_16_out, subtractor_2_out[26]);
  not not_17 (not_17_out, subtractor_2_out[27]);
  not not_18 (not_18_out, subtractor_2_out[28]);
  not not_19 (not_19_out, subtractor_2_out[29]);
  not not_20 (not_20_out, subtractor_2_out[10]);
  not not_21 (not_21_out, subtractor_2_out[11]);
  not not_22 (not_22_out, subtractor_2_out[12]);
  not not_23 (not_23_out, subtractor_2_out[13]);
  not not_24 (not_24_out, subtractor_2_out[14]);
  not not_25 (not_25_out, subtractor_2_out[15]);
  not not_26 (not_26_out, subtractor_2_out[16]);
  not not_27 (not_27_out, subtractor_2_out[17]);
  not not_28 (not_28_out, subtractor_2_out[18]);
  not not_29 (not_29_out, subtractor_2_out[19]);
  not not_30 (not_30_out, subtractor_2_out[20]);
  not not_31 (not_31_out, subtractor_2_out[21]);
  not not_32 (not_32_out, subtractor_2_out[22]);
  and and_2 (and_2_out, not_1_out, not_2_out, not_5_out, not_6_out, not_7_out, not_8_out, not_9_out, not_10_out, not_11_out, not_12_out, not_20_out, not_21_out, not_22_out, not_23_out, not_24_out, not_25_out, not_26_out, not_27_out, not_28_out, not_29_out, not_30_out, not_31_out, not_32_out, not_13_out, not_14_out, not_15_out, not_16_out, not_17_out, not_18_out, not_19_out, not_3_out, not_4_out);
endmodule

module ALU_Ctr (
  input  [5:0] Function,
  input  [5:0] OP_Code,
  output [2:0] ALU_OP
);

  wire and_1_out, not_1_out, not_2_out, not_3_out;
  wire [2:0] multiplexer_2_out;

  not not_1 (not_1_out, OP_Code[0]);
  and and_1 (and_1_out, not_1_out, not_2_out, not_3_out);
  not not_2 (not_2_out, OP_Code[1]);
  not not_3 (not_3_out, OP_Code[2]);
  Multiplexer #(.select(3), .width(3), .enable("false")) multiplexer_1 (
    .in0(3'b000), .in1(3'b001), .in2(3'b010), .in3(3'b100), .in4(3'b101), .in5(3'b010), .in6(3'b010),
    .in7(3'b011), .out(ALU_OP), .sel(multiplexer_2_out));
  Multiplexer #(.width(3), .enable("false")) multiplexer_2 (
    .in0(OP_Code[2:0]), .in1(Function[2:0]), .out(multiplexer_2_out), .sel(and_1_out));
endmodule

// Control Unit
module Ctr_Unit (
  input  [31:0] Instruction,
  output Reg_Ds,
  output Reg_Write,
  output ALU_Src,
  output Mem_to_Reg,
  output Mem_Write,
  output Ext_Op,
  output Branch,
  output Jump
);

  wire and_2_out, and_3_out, and_4_out, and_5_out, and_6_out, and_7_out, and_8_out, and_9_out, not_1_out,
       not_2_out, not_3_out, not_4_out, not_5_out, not_6_out, not_7_out, not_8_out, not_9_out, not_10_out,
       not_11_out, not_12_out, not_13_out, not_14_out, not_15_out, not_16_out, or_1_out;

  not not_1 (not_1_out, Instruction[26]);
  not not_2 (not_2_out, Instruction[27]);
  not not_3 (not_3_out, Instruction[28]);
  not not_4 (not_4_out, Instruction[29]);
  and and_1 (Jump, not_1_out, not_2_out, not_3_out, not_4_out, Instruction[30], Instruction[31]);
  not not_5 (not_5_out, Instruction[26]);
  not not_6 (not_6_out, Instruction[27]);
  not not_7 (not_7_out, Instruction[28]);
  not not_8 (not_8_out, Instruction[27]);
  not not_9 (not_9_out, Instruction[28]);
  not not_10 (not_10_out, Instruction[26]);
  not not_11 (not_11_out, Instruction[28]);
  not not_12 (not_12_out, Instruction[28]);
  not not_13 (not_13_out, Instruction[26]);
  not not_14 (not_14_out, Instruction[27]);
  not not_15 (not_15_out, Instruction[27]);
  not not_16 (not_16_out, Instruction[26]);
  and and_2 (and_2_out, not_5_out, not_6_out, not_7_out);
  and and_3 (and_3_out, Instruction[26], not_8_out, not_9_out);
  and and_4 (and_4_out, not_10_out, Instruction[27], not_11_out);
  and and_5 (and_5_out, Instruction[26], Instruction[27], not_12_out);
  and and_6 (and_6_out, not_13_out, not_14_out, Instruction[28]);
  and and_7 (and_7_out, Instruction[26], not_15_out, Instruction[28]);
  and and_8 (and_8_out, not_16_out, Instruction[27], Instruction[28]);
  and and_9 (and_9_out, Instruction[26], Instruction[27], Instruction[28]);
  buf or_1 (or_1_out, and_2_out);  // OR_Gate
  or or_2 (Reg_Write, and_2_out, and_3_out, and_4_out, and_5_out, and_6_out, and_8_out);
  or or_3 (ALU_Src, and_3_out, and_4_out, and_5_out, and_6_out, and_8_out, and_7_out);
  buf or_4 (Mem_to_Reg, and_8_out);  // OR_Gate
  buf or_5 (Mem_Write, and_7_out);  // OR_Gate
  or or_6 (Ext_Op, and_7_out, and_8_out);
  buf or_7 (Branch, and_9_out);  // OR_Gate
  or or_8 (Reg_Ds, 1'b0, or_1_out);

  // Notes on the sheet:
  //   Jump(110000)
  //   Ori(001)
  //   Addi(010)
  //   Muli(011)
  //   Divi(100)
  //   Sw(101)
  //   Lw(110)
  //   Beq(111)
  //   R-Type(000)
endmodule

module Reg_File (
  input  [4:0] Write_Reg,
  input  [4:0] Read_Reg_1,
  input  [31:0] Data,
  input  Reg_Write,
  input  [4:0] Read_Reg_2,
  output [31:0] Read_Data_1,
  output [31:0] Read_Data_2
);

  wire and_1_out, and_2_out, and_3_out, and_4_out, and_5_out, and_6_out, and_7_out, and_8_out, Clock_out,
       decoder_1_out0, decoder_1_out1, decoder_1_out2, decoder_1_out3, decoder_1_out4, decoder_1_out5,
       decoder_1_out6, decoder_1_out7;
  wire [31:0] register_1_q, register_2_q, register_3_q, register_4_q, register_5_q, register_6_q,
       register_7_q, register_8_q;

  Decoder #(.select(3), .enable("false")) decoder_1 (
    .out0(decoder_1_out0), .out1(decoder_1_out1), .out2(decoder_1_out2), .out3(decoder_1_out3),
    .out4(decoder_1_out4), .out5(decoder_1_out5), .out6(decoder_1_out6), .out7(decoder_1_out7),
    .sel(Write_Reg[2:0]));
  Clock Clock (.out(Clock_out));
  and and_1 (and_1_out, Reg_Write, decoder_1_out0);
  and and_2 (and_2_out, Reg_Write, decoder_1_out1);
  and and_3 (and_3_out, Reg_Write, decoder_1_out2);
  and and_4 (and_4_out, Reg_Write, decoder_1_out3);
  Register #(.width(32)) register_1 (.D(Data), .en(and_1_out), .Q(register_1_q), .clk(Clock_out), .clr(1'b0));
  Register #(.width(32)) register_2 (.D(Data), .en(and_2_out), .Q(register_2_q), .clk(Clock_out), .clr(1'b0));
  Register #(.width(32)) register_3 (.D(Data), .en(and_3_out), .Q(register_3_q), .clk(Clock_out), .clr(1'b0));
  Register #(.width(32)) register_4 (.D(Data), .en(and_4_out), .Q(register_4_q), .clk(Clock_out), .clr(1'b0));
  and and_5 (and_5_out, Reg_Write, decoder_1_out4);
  and and_6 (and_6_out, Reg_Write, decoder_1_out5);
  and and_7 (and_7_out, Reg_Write, decoder_1_out6);
  and and_8 (and_8_out, Reg_Write, decoder_1_out7);
  Register #(.width(32)) register_5 (.D(Data), .en(and_5_out), .Q(register_5_q), .clk(Clock_out), .clr(1'b0));
  Register #(.width(32)) register_6 (.D(Data), .en(and_6_out), .Q(register_6_q), .clk(Clock_out), .clr(1'b0));
  Register #(.width(32)) register_7 (.D(Data), .en(and_7_out), .Q(register_7_q), .clk(Clock_out), .clr(1'b0));
  Register #(.width(32)) register_8 (.D(Data), .en(and_8_out), .Q(register_8_q), .clk(Clock_out), .clr(1'b0));
  Multiplexer #(.select(3), .width(32), .enable("false")) multiplexer_1 (
    .in0(register_1_q), .in1(register_2_q), .in2(register_3_q), .in3(register_4_q), .in4(register_5_q),
    .in5(register_6_q), .in6(register_7_q), .in7(register_8_q), .out(Read_Data_1), .sel(Read_Reg_1[2:0]));
  Multiplexer #(.select(3), .width(32), .enable("false")) multiplexer_2 (
    .in0(register_1_q), .in1(register_2_q), .in2(register_3_q), .in3(register_4_q), .in4(register_5_q),
    .in5(register_6_q), .in6(register_7_q), .in7(register_8_q), .out(Read_Data_2), .sel(Read_Reg_2[2:0]));
endmodule

module Extension (
  input  Ext_Op,
  input  [15:0] Imm,
  output [31:0] Ext
);

  Multiplexer #(.width(32), .enable("false")) multiplexer_1 (
    .in0({{16{1'b0}}, Imm}), .in1({{17{Imm[15]}}, Imm[14:0]}), .out(Ext), .sel(Ext_Op));
endmodule

module Extention_Jump (
  input  [25:0] Target,
  output [31:0] Ext_Jump
);


  assign Ext_Jump = {{6{1'b0}}, Target};
endmodule
